// Logisim project Tasks_Lab3_Semenova.circ as structural Verilog: 2 circuits, main circuit Task1
module Task1 (
  input  bit4,
  input  bit3,
  input  bit2,
  input  bit1,
  input  bit0,
  output out_6
);

  wire and_1_out, and_2_out, and_3_out, or_1_out;

  and and_1 (and_1_out, bit2, bit1);
  and and_2 (and_2_out, bit2, bit0);
  or or_1 (or_1_out, bit3, and_1_out, and_2_out);
  and and_3 (and_3_out, bit4, or_1_out);
  not not_1 (out_6, and_3_out);

  // Notes on the sheet:
  //   На выходе "0", когда на входе число, большее 21
endmodule

module Task2 (
  input  bit4,
  input  bit3,
  input  bit2,
  input  bit1,
  input  bit0,
  output out_6
);

  wire and_1_out, and_2_out, and_3_out, and_4_out, not_1_out, not_2_out, not_3_out, not_4_out, not_5_out,
       or_1_out;

  not not_1 (not_1_out, bit4);
  not not_2 (not_2_out, bit3);
  not not_3 (not_3_out, bit2);
  not not_4 (not_4_out, bit1);
  not not_5 (not_5_out, bit0);
  and and_1 (and_1_out, not_1_out, not_2_out);
  and and_2 (and_2_out, not_2_out, not_3_out);
  and and_3 (and_3_out, not_3_out, not_4_out);
  and and_4 (and_4_out, not_4_out, not_5_out);
  or or_1 (or_1_out, and_1_out, and_2_out, and_3_out, and_4_out);
  not not_6 (out_6, or_1_out);

  // Notes on the sheet:
  //   На выходе "1", когда на выходах нет ни одной пары нулей, идущих подряд
endmodule
