// Logisim project Lab4_Sem.circ as structural Verilog: 6 circuits, main circuit 1
module _1 (
  input  in_1,
  input  in_2,
  output out_3,
  output out_4
);

  nor nor_1 (out_3, in_1, out_4);
  nor nor_2 (out_4, out_3, in_2);

  // Notes on the sheet:
  //   Асинхронный RS триггер с прямыми входами
endmodule

module _2 (
  input  r,
  input  s,
  output out_3,
  output out_4
);

  nand nand_1 (out_3, r, out_4);
  nand nand_2 (out_4, out_3, s);

  // Notes on the sheet:
  //   Асинхронный RS триггер с инверсными входами
endmodule

module _3 (
  input  S,
  input  C,
  input  R,
  output out_4,
  output out_5
);

  wire nand_1_out, nand_2_out;

  nand nand_1 (nand_1_out, S, C);
  nand nand_2 (nand_2_out, C, R);
  nand nand_3 (out_4, nand_1_out, out_5);
  nand nand_4 (out_5, out_4, nand_2_out);

  // Notes on the sheet:
  //   Синхронный RS триггер
endmodule

module _4 (
  input  S,
  input  R,
  output out_3,
  output out_4
);

  wire nand_1_out, nand_2_out;

  nand nand_1 (nand_1_out, S, S);
  nand nand_2 (nand_2_out, nand_1_out, R);
  nand nand_3 (out_3, nand_1_out, out_4);
  nand nand_4 (out_4, out_3, nand_2_out);

  // Notes on the sheet:
  //   S-триггер
endmodule

module _5 (
  input  S,
  input  R,
  output out_3,
  output out_4
);

  wire nand_1_out, nand_2_out;

  nand nand_1 (nand_1_out, S, nand_2_out);
  nand nand_2 (nand_2_out, R, R);
  nand nand_3 (out_3, nand_1_out, out_4);
  nand nand_4 (out_4, out_3, nand_2_out);

  // Notes on the sheet:
  //   R-триггер
endmodule

module _6 (
  input  S,
  input  R,
  output out_3,
  output out_4
);

  wire nand_1_out, nand_2_out, nand_3_out, nand_4_out;

  nand nand_1 (nand_1_out, S, S);
  nand nand_2 (nand_2_out, R, R);
  nand nand_3 (nand_3_out, S, nand_2_out);
  nand nand_4 (nand_4_out, nand_1_out, R);
  nand nand_5 (out_3, nand_3_out, out_4);
  nand nand_6 (out_4, out_3, nand_4_out);

  // Notes on the sheet:
  //   E-триггер
endmodule
