// Logisim project L5_Semenova.circ as structural Verilog: 3 circuits, main circuit dtrigger
module dtrigger (
  input  D,
  input  C,
  output out_3,
  output out_4
);

  wire nand_1_out, nand_2_out;

  nand nand_1 (nand_1_out, D, C);
  nand nand_2 (nand_2_out, nand_1_out, C);
  nand nand_3 (out_3, nand_1_out, out_4);
  nand nand_4 (out_4, out_3, nand_2_out);

  // Notes on the sheet:
  //   D триггер
endmodule

module Ttrigger (
  input  t,
  input  c,
  output out_3
);

  wire nand_1_out, nand_2_out, nand_3_out, nand_5_out;

  nand nand_1 (nand_1_out, t, c);
  nand nand_2 (nand_2_out, nand_5_out, nand_1_out);
  nand nand_3 (nand_3_out, nand_2_out, nand_1_out);
  not nand_4 (out_3, nand_2_out);  // NAND_Gate
  nand nand_5 (nand_5_out, out_3, nand_3_out);

  // Notes on the sheet:
  //   T триггер
endmodule

module JKtrigger (
  input  j,
  input  c,
  input  k,
  output out_4,
  output out_5
);

  wire nand_1_out, nand_2_out, nand_3_out, nand_4_out, nand_5_out, nand_6_out;

  nand nand_1 (nand_1_out, out_5, j, c);
  nand nand_2 (nand_2_out, c, k, out_4);
  nand nand_3 (nand_3_out, nand_1_out, nand_4_out);
  nand nand_4 (nand_4_out, nand_3_out, nand_2_out);
  nand nand_5 (nand_5_out, nand_1_out, nand_3_out);
  nand nand_6 (nand_6_out, nand_4_out, nand_2_out);
  nand nand_7 (out_4, nand_5_out, out_5);
  nand nand_8 (out_5, out_4, nand_6_out);

  // Notes on the sheet:
  //   JK триггер
endmodule
