// Logisim project L6_Semenova.circ as structural Verilog: 4 circuits, main circuit Схема сравнения
module \Схема_сравнения  (
  input  X1,
  input  X2,
  output Y
);

  wire \И_2_out , \И_out , \НЕ_2_out , \НЕ_out ;

  not \u_НЕ  (\НЕ_out , X1);
  not \u_НЕ_2  (\НЕ_2_out , X2);
  and \u_И  (\И_out , \НЕ_out , X2);
  and \u_И_2  (\И_2_out , X1, \НЕ_2_out );
  or \u_ИЛИ  (Y, \И_out , \И_2_out );

  // Notes on the sheet:
  //   Схема сравнения
endmodule

module \Полусумматор  (
  input  X1,
  input  X2,
  output \Старший_разряд ,
  output \Младший_разряд 
);

  \Схема_сравнения  \u_Схема_сравнения  (.X1(X1), .X2(X2), .Y(\Младший_разряд ));
  and \u_И  (\Старший_разряд , X1, X2);

  // Notes on the sheet:
  //   Полусумматор
endmodule

module \Сумматор  (
  input  X1,
  input  X2,
  input  P1,
  output \Перенос ,
  output \Младший_разряд_суммы 
);

  wire \Полусумматор_2_старший_разряд , \Полусумматор_младший_разряд , \Полусумматор_старший_разряд ;

  \Полусумматор  \u_Полусумматор  (
    .X1(X1), .X2(X2), .\Старший_разряд (\Полусумматор_старший_разряд ),
    .\Младший_разряд (\Полусумматор_младший_разряд ));
  \Полусумматор  \u_Полусумматор_2  (
    .X1(\Полусумматор_младший_разряд ), .X2(P1), .\Старший_разряд (\Полусумматор_2_старший_разряд ),
    .\Младший_разряд (\Младший_разряд_суммы ));
  or \u_ИЛИ  (\Перенос , \Полусумматор_старший_разряд , \Полусумматор_2_старший_разряд );

  // Notes on the sheet:
  //   СУММАТОР
endmodule

module \схема_из_4х_сумматоров  (
  input  X4,
  input  Y4,
  input  X3,
  input  Y3,
  input  X2,
  input  Y2,
  input  X1,
  input  Y1,
  input  P0,
  output S5,
  output S4,
  output S3,
  output S2,
  output S1
);

  wire \сумматор_1_перенос , \сумматор_2_перенос , \сумматор_3_перенос ;

  \Сумматор  \u_сумматор_1  (.X1(X1), .X2(Y1), .P1(P0), .\Перенос (\сумматор_1_перенос ), .\Младший_разряд_суммы (S1));
  \Сумматор  \u_сумматор_2  (
    .X1(X3), .X2(Y3), .P1(\сумматор_3_перенос ), .\Перенос (\сумматор_2_перенос ), .\Младший_разряд_суммы (S3));
  \Сумматор  \u_сумматор_3  (
    .X1(X2), .X2(Y2), .P1(\сумматор_1_перенос ), .\Перенос (\сумматор_3_перенос ), .\Младший_разряд_суммы (S2));
  \Сумматор  \u_сумматор_4  (.X1(X4), .X2(Y4), .P1(\сумматор_2_перенос ), .\Перенос (S5), .\Младший_разряд_суммы (S4));

  // Notes on the sheet:
  //   P2
  //   SM
  //   P1
  //   SM
  //   P3
  //   SM
  //   P4
  //   SM
endmodule
