// Logisim project L7_Semenova.circ as structural Verilog: 4 circuits, main circuit 2х канальный мультиплексор
module \_2х_канальный_мультиплексор  (
  input  a,
  input  b,
  input  sel,
  output out
);

  wire and_1_out, and_2_out, not_1_out;

  not not_1 (not_1_out, sel);
  and and_1 (and_1_out, a, not_1_out);
  and and_2 (and_2_out, b, sel);
  or or_1 (out, and_1_out, and_2_out);
endmodule

module \_4х_канальный_мультиплексор  (
  input  A0,
  input  A1,
  input  D0,
  input  D1,
  input  D2,
  input  D3,
  output Y
);

  wire not_1_out, not_2_out, \И_2_out , \И_3_out , \И_4_out , \И_out ;

  not not_1 (not_1_out, A0);
  not not_2 (not_2_out, A1);
  and \u_И  (\И_out , not_1_out, not_2_out, D0);
  and \u_И_2  (\И_2_out , not_2_out, A0, D1);
  and \u_И_3  (\И_3_out , not_1_out, D2, A1);
  and \u_И_4  (\И_4_out , A0, D3, A1);
  or \u_ИЛИ  (Y, \И_out , \И_2_out , \И_3_out , \И_4_out );

  // Notes on the sheet:
  //   Адрес
  //   МУЛЬТИПЛЕКСОР
  //   Информационный вход
endmodule

module \_16ти_канальный_мультиплексор  (
  input  D0,
  input  D1,
  input  D2,
  input  D3,
  input  D4,
  input  D5,
  input  D6,
  input  D7,
  input  D8,
  input  D9,
  input  D10,
  input  D11,
  input  D12,
  input  D13,
  input  D14,
  input  D15,
  input  A0,
  input  A1,
  input  A2,
  input  A3,
  output out_21
);

  wire MUX_3_y, MUX_y, \n4х_канальный_мультиплексор_1_y ;

  \_4х_канальный_мультиплексор  MUX (.A0(D0), .A1(D1), .D0(D2), .D1(D3), .D2(A0), .D3(A1), .Y(MUX_y));
  \_4х_канальный_мультиплексор  MUX_2 (.A0(D4), .A1(D5), .D0(D6), .D1(D7), .D2(A0), .D3(A1), .Y(MUX_y));
  \_4х_канальный_мультиплексор  \u_4х_канальный_мультиплексор_1  (
    .A0(D8), .A1(D8), .D0(D10), .D1(D11), .D2(A0), .D3(A1), .Y(\n4х_канальный_мультиплексор_1_y ));
  \_4х_канальный_мультиплексор  MUX_3 (.A0(D12), .A1(D13), .D0(D14), .D1(D15), .D2(A0), .D3(A1), .Y(MUX_3_y));
  \_4х_канальный_мультиплексор  MUX_4 (
    .A0(MUX_y), .A1(MUX_y), .D0(\n4х_канальный_мультиплексор_1_y ), .D1(MUX_3_y), .D2(A2), .D3(A3), .Y(out_21));

  assign D9 = D8;

  // Notes on the sheet:
  //   Каскадное соединение мультиплексоров (16-1)
endmodule

module \демультиплексор  (
  input  in,
  input  sel,
  output a,
  output b
);

  wire not_1_out;

  not not_1 (not_1_out, sel);
  and and_1 (a, in, not_1_out);
  and and_2 (b, in, sel);

  // Notes on the sheet:
  //   Демультиплексор
endmodule
